// Logisim project Device.circ as structural Verilog: 44 circuits, main circuit main
module main (
);


  // Notes on the sheet:
  //   CHOBNGMJEFLAIDPK
  //   JMFBDLIGHPOENACK
  //   0 J srl   Logic
  //   1 M sw   Memory
  //   2 F andi   Logic
  //   3 B addi   Arith
  //   4 D subi   Arith
  //   5 L lw   Memory
  //   6 I sll   Logic
  //   7 G or   Logic
  //   8 H ori   Logic
  //   9 P j   Control
  //   10 O bneq   Control
  //   11 E and   Logic
  //   12 N beq   Control
  //   13 A add   Arith
  //   14 C sub   Arith
  //   15 K nor   Logic
endmodule

// AND2
module AND1bit2x1 (
  input  [1:0] in_1,
  output out_2
);

  // _7408 7408_1: pin names not known; wires that end beside it: in_1[0], in_1[1], out_2, 1'b0, 1'b1
endmodule

// AND4
module AND1bit4x1 (
  input  [3:0] in_1,
  output out_2
);

  wire [1:0] and1bit2x1_1_out_2;

  AND1bit2x1 and1bit2x1_1 (.in_1(in_1[1:0]), .out_2(and1bit2x1_1_out_2[0]));
  AND1bit2x1 and1bit2x1_2 (.in_1(in_1[3:2]), .out_2(and1bit2x1_1_out_2[1]));
  AND1bit2x1 and1bit2x1_3 (.in_1(and1bit2x1_1_out_2), .out_2(out_2));
endmodule

// AND8
module AND1bit8x1 (
  input  [7:0] in_1,
  output out_2
);

  wire [1:0] and1bit4x1_1_out_2;

  AND1bit4x1 and1bit4x1_1 (.in_1(in_1[3:0]), .out_2(and1bit4x1_1_out_2[0]));
  AND1bit4x1 and1bit4x1_2 (.in_1(in_1[7:4]), .out_2(and1bit4x1_1_out_2[1]));
  AND1bit2x1 and1bit2x1_1 (.in_1(and1bit4x1_1_out_2), .out_2(out_2));
endmodule

// AND16
module AND1bit16x1 (
  input  [15:0] in_1,
  output out_2
);

  wire [1:0] and1bit8x1_1_out_2;

  AND1bit8x1 and1bit8x1_1 (.in_1(in_1[7:0]), .out_2(and1bit8x1_1_out_2[0]));
  AND1bit8x1 and1bit8x1_2 (.in_1(in_1[15:8]), .out_2(and1bit8x1_1_out_2[1]));
  AND1bit2x1 and1bit2x1_1 (.in_1(and1bit8x1_1_out_2), .out_2(out_2));
endmodule

// OR2
module OR1bit2x1 (
  input  [1:0] in_1,
  output out_2
);

  // _7432 7432_1: pin names not known; wires that end beside it: in_1[0], in_1[1], out_2, 1'b0, 1'b1
endmodule

// OR4
module OR1bit4x1 (
  input  [3:0] in_1,
  output out_2
);

  wire [1:0] or1bit2x1_1_out_2;

  OR1bit2x1 or1bit2x1_1 (.in_1(in_1[1:0]), .out_2(or1bit2x1_1_out_2[0]));
  OR1bit2x1 or1bit2x1_2 (.in_1(in_1[3:2]), .out_2(or1bit2x1_1_out_2[1]));
  OR1bit2x1 or1bit2x1_3 (.in_1(or1bit2x1_1_out_2), .out_2(out_2));
endmodule

// OR8
module OR1bit8x1 (
  input  [7:0] in_1,
  output out_2
);

  wire [1:0] or1bit4x1_1_out_2;

  OR1bit4x1 or1bit4x1_1 (.in_1(in_1[3:0]), .out_2(or1bit4x1_1_out_2[0]));
  OR1bit4x1 or1bit4x1_2 (.in_1(in_1[7:4]), .out_2(or1bit4x1_1_out_2[1]));
  OR1bit2x1 or1bit2x1_1 (.in_1(or1bit4x1_1_out_2), .out_2(out_2));
endmodule

// OR12
module OR1bit12x1 (
  input  [11:0] in_1,
  output out_2
);

  wire [1:0] or1bit4x1_1_out_2;

  OR1bit4x1 or1bit4x1_1 (.in_1(in_1[3:0]), .out_2(or1bit4x1_1_out_2[0]));
  OR1bit8x1 or1bit8x1_1 (.in_1(in_1[11:4]), .out_2(or1bit4x1_1_out_2[1]));
  OR1bit2x1 or1bit2x1_1 (.in_1(or1bit4x1_1_out_2), .out_2(out_2));
endmodule

// OR16
module OR1bit16x1 (
  input  [15:0] in_1,
  output out_2
);

  wire [1:0] or1bit8x1_1_out_2;

  OR1bit8x1 or1bit8x1_1 (.in_1(in_1[7:0]), .out_2(or1bit8x1_1_out_2[0]));
  OR1bit8x1 or1bit8x1_2 (.in_1(in_1[15:8]), .out_2(or1bit8x1_1_out_2[1]));
  OR1bit2x1 or1bit2x1_1 (.in_1(or1bit8x1_1_out_2), .out_2(out_2));
endmodule

// OR19
module OR1bit19x1 (
  input  [18:0] in_1,
  output out_2
);

  wire [3:3] or1bit16x1_1_out_2;

  OR1bit16x1 or1bit16x1_1 (.in_1(in_1[18:3]), .out_2(or1bit16x1_1_out_2[3]));
  OR1bit4x1 or1bit4x1_1 (.in_1({or1bit16x1_1_out_2[3], in_1[2:0]}), .out_2(out_2));
endmodule

// M4
module MUX4bit2x1 (
  input  S,
  input  [3:0] Data0,
  input  [3:0] Data1,
  output [3:0] DataOut
);

  // _74157 74157_1: pin names not known; wires that end beside it: S, Data0[0], Data1[0], DataOut[0], Data0[1], Data1[1], DataOut[1], 1'b0, 1'b1, 1'b0, Data0[3], Data1[3], DataOut[3], Data0[2], Data1[2], DataOut[2]
endmodule

// M3
module MUX3bit2x1 (
  input  S,
  input  [2:0] Data0,
  input  [2:0] Data1,
  output [2:0] DataOut
);

  wire n74157_1_p11, n74157_1_p12, n74157_1_p13;

  // _74157 74157_1: pin names not known; wires that end beside it: S, Data0[0], Data1[0], DataOut[0], Data0[1], Data1[1], DataOut[1], 1'b0, 1'b1, 1'b0, n74157_1_p11, n74157_1_p12, n74157_1_p13, Data0[2], Data1[2], DataOut[2], n74157_1_p11, n74157_1_p12, n74157_1_p13
endmodule

// M12
module MUX12bit2x1 (
  input  S,
  input  [11:0] Data0,
  input  [11:0] Data1,
  output [11:0] DataOut
);

  MUX4bit2x1 mux4bit2x1_1 (.S(S), .Data0(Data0[3:0]), .Data1(Data1[3:0]), .DataOut(DataOut[3:0]));
  MUX4bit2x1 mux4bit2x1_2 (.S(S), .Data0(Data0[7:4]), .Data1(Data1[7:4]), .DataOut(DataOut[7:4]));
  MUX4bit2x1 mux4bit2x1_3 (.S(S), .Data0(Data0[11:8]), .Data1(Data1[11:8]), .DataOut(DataOut[11:8]));
endmodule

// M19
module MUX19bit2x1 (
  input  S,
  input  [18:0] Data0,
  input  [18:0] Data1,
  output [18:0] DataOut
);

  MUX4bit2x1 mux4bit2x1_1 (.S(S), .Data0(Data0[3:0]), .Data1(Data1[3:0]), .DataOut(DataOut[3:0]));
  MUX4bit2x1 mux4bit2x1_2 (.S(S), .Data0(Data0[7:4]), .Data1(Data1[7:4]), .DataOut(DataOut[7:4]));
  MUX4bit2x1 mux4bit2x1_3 (.S(S), .Data0(Data0[11:8]), .Data1(Data1[11:8]), .DataOut(DataOut[11:8]));
  MUX4bit2x1 mux4bit2x1_4 (.S(S), .Data0(Data0[15:12]), .Data1(Data1[15:12]), .DataOut(DataOut[15:12]));
  MUX3bit2x1 mux3bit2x1_1 (.S(S), .Data0(Data0[18:16]), .Data1(Data1[18:16]), .DataOut(DataOut[18:16]));
endmodule

// M32
module MUX32bit2x1 (
  input  S,
  input  [31:0] Data0,
  input  [31:0] Data1,
  output [31:0] DataOut
);

  MUX4bit2x1 mux4bit2x1_1 (.S(S), .Data0(Data0[3:0]), .Data1(Data1[3:0]), .DataOut(DataOut[3:0]));
  MUX4bit2x1 mux4bit2x1_2 (.S(S), .Data0(Data0[7:4]), .Data1(Data1[7:4]), .DataOut(DataOut[7:4]));
  MUX4bit2x1 mux4bit2x1_3 (.S(S), .Data0(Data0[11:8]), .Data1(Data1[11:8]), .DataOut(DataOut[11:8]));
  MUX4bit2x1 mux4bit2x1_4 (.S(S), .Data0(Data0[15:12]), .Data1(Data1[15:12]), .DataOut(DataOut[15:12]));
  MUX4bit2x1 mux4bit2x1_5 (.S(S), .Data0(Data0[19:16]), .Data1(Data1[19:16]), .DataOut(DataOut[19:16]));
  MUX4bit2x1 mux4bit2x1_6 (.S(S), .Data0(Data0[23:20]), .Data1(Data1[23:20]), .DataOut(DataOut[23:20]));
  MUX4bit2x1 mux4bit2x1_7 (.S(S), .Data0(Data0[27:24]), .Data1(Data1[27:24]), .DataOut(DataOut[27:24]));
  MUX4bit2x1 mux4bit2x1_8 (.S(S), .Data0(Data0[31:28]), .Data1(Data1[31:28]), .DataOut(DataOut[31:28]));
endmodule

// M31
module MUX31bit2x1 (
  input  S,
  input  [30:0] Data0,
  input  [30:0] Data1,
  output [30:0] DataOut
);

  MUX4bit2x1 mux4bit2x1_1 (.S(S), .Data0(Data0[3:0]), .Data1(Data1[3:0]), .DataOut(DataOut[3:0]));
  MUX4bit2x1 mux4bit2x1_2 (.S(S), .Data0(Data0[7:4]), .Data1(Data1[7:4]), .DataOut(DataOut[7:4]));
  MUX4bit2x1 mux4bit2x1_3 (.S(S), .Data0(Data0[11:8]), .Data1(Data1[11:8]), .DataOut(DataOut[11:8]));
  MUX4bit2x1 mux4bit2x1_4 (.S(S), .Data0(Data0[15:12]), .Data1(Data1[15:12]), .DataOut(DataOut[15:12]));
  MUX4bit2x1 mux4bit2x1_5 (.S(S), .Data0(Data0[19:16]), .Data1(Data1[19:16]), .DataOut(DataOut[19:16]));
  MUX4bit2x1 mux4bit2x1_6 (.S(S), .Data0(Data0[23:20]), .Data1(Data1[23:20]), .DataOut(DataOut[23:20]));
  MUX4bit2x1 mux4bit2x1_7 (.S(S), .Data0(Data0[27:24]), .Data1(Data1[27:24]), .DataOut(DataOut[27:24]));
  MUX3bit2x1 mux3bit2x1_1 (.S(S), .Data0(Data0[30:28]), .Data1(Data1[30:28]), .DataOut(DataOut[30:28]));
endmodule

// M28
module MUX28bit2x1 (
  input  S,
  input  [27:0] Data0,
  input  [27:0] Data1,
  output [27:0] DataOut
);

  MUX4bit2x1 mux4bit2x1_1 (.S(S), .Data0(Data0[3:0]), .Data1(Data1[3:0]), .DataOut(DataOut[3:0]));
  MUX4bit2x1 mux4bit2x1_2 (.S(S), .Data0(Data0[7:4]), .Data1(Data1[7:4]), .DataOut(DataOut[7:4]));
  MUX4bit2x1 mux4bit2x1_3 (.S(S), .Data0(Data0[11:8]), .Data1(Data1[11:8]), .DataOut(DataOut[11:8]));
  MUX4bit2x1 mux4bit2x1_4 (.S(S), .Data0(Data0[15:12]), .Data1(Data1[15:12]), .DataOut(DataOut[15:12]));
  MUX4bit2x1 mux4bit2x1_5 (.S(S), .Data0(Data0[19:16]), .Data1(Data1[19:16]), .DataOut(DataOut[19:16]));
  MUX4bit2x1 mux4bit2x1_6 (.S(S), .Data0(Data0[23:20]), .Data1(Data1[23:20]), .DataOut(DataOut[23:20]));
  MUX4bit2x1 mux4bit2x1_7 (.S(S), .Data0(Data0[27:24]), .Data1(Data1[27:24]), .DataOut(DataOut[27:24]));
endmodule

// M25
module MUX25bit2x1 (
  input  S,
  input  [24:0] Data0,
  input  [24:0] Data1,
  output [24:0] DataOut
);

  MUX4bit2x1 mux4bit2x1_1 (.S(S), .Data0(Data0[3:0]), .Data1(Data1[3:0]), .DataOut(DataOut[3:0]));
  MUX4bit2x1 mux4bit2x1_2 (.S(S), .Data0(Data0[7:4]), .Data1(Data1[7:4]), .DataOut(DataOut[7:4]));
  MUX4bit2x1 mux4bit2x1_3 (.S(S), .Data0(Data0[11:8]), .Data1(Data1[11:8]), .DataOut(DataOut[11:8]));
  MUX4bit2x1 mux4bit2x1_4 (.S(S), .Data0(Data0[15:12]), .Data1(Data1[15:12]), .DataOut(DataOut[15:12]));
  MUX3bit2x1 mux3bit2x1_1 (.S(S), .Data0(Data0[18:16]), .Data1(Data1[18:16]), .DataOut(DataOut[18:16]));
  MUX3bit2x1 mux3bit2x1_2 (.S(S), .Data0(Data0[21:19]), .Data1(Data1[21:19]), .DataOut(DataOut[21:19]));
  MUX3bit2x1 mux3bit2x1_3 (.S(S), .Data0(Data0[24:22]), .Data1(Data1[24:22]), .DataOut(DataOut[24:22]));
endmodule

// M22
module MUX22bit2x1 (
  input  S,
  input  [21:0] Data0,
  input  [21:0] Data1,
  output [21:0] DataOut
);

  MUX4bit2x1 mux4bit2x1_1 (.S(S), .Data0(Data0[3:0]), .Data1(Data1[3:0]), .DataOut(DataOut[3:0]));
  MUX4bit2x1 mux4bit2x1_2 (.S(S), .Data0(Data0[7:4]), .Data1(Data1[7:4]), .DataOut(DataOut[7:4]));
  MUX4bit2x1 mux4bit2x1_3 (.S(S), .Data0(Data0[11:8]), .Data1(Data1[11:8]), .DataOut(DataOut[11:8]));
  MUX4bit2x1 mux4bit2x1_4 (.S(S), .Data0(Data0[15:12]), .Data1(Data1[15:12]), .DataOut(DataOut[15:12]));
  MUX3bit2x1 mux3bit2x1_1 (.S(S), .Data0(Data0[18:16]), .Data1(Data1[18:16]), .DataOut(DataOut[18:16]));
  MUX3bit2x1 mux3bit2x1_2 (.S(S), .Data0(Data0[21:19]), .Data1(Data1[21:19]), .DataOut(DataOut[21:19]));
endmodule

// A3
module Adder3bit (
  input  Cin,
  input  [2:0] Data0,
  input  [2:0] Data1,
  output [2:0] DataOut,
  output Cout
);

  // _7483 7483_1: pin names not known; wires that end beside it: 1'b0, DataOut[2], Data0[2], Data1[2], 1'b1, DataOut[1], Data1[1], Data0[1], 1'b0, Cout, Cin, 1'b0, Data1[0], Data0[0], DataOut[0]
endmodule

// A4
module Adder4bit (
  input  Cin,
  input  [3:0] Data0,
  input  [3:0] Data1,
  output [3:0] DataOut,
  output Cout
);

  // _7483 7483_1: pin names not known; wires that end beside it: Data0[3], DataOut[2], Data0[2], Data1[2], 1'b1, DataOut[1], Data1[1], Data0[1], Data1[3], DataOut[3], Cout, Cin, 1'b0, Data1[0], Data0[0], DataOut[0]
endmodule

// A12
module Adder12bit (
  input  Cin,
  input  [11:0] Data0,
  input  [11:0] Data1,
  output [11:0] DataOut,
  output Cout
);

  wire adder4bit_1_cout, adder4bit_2_cout;

  Adder4bit adder4bit_1 (
    .Data0(Data0[3:0]), .Data1(Data1[3:0]), .Cin(Cin), .Cout(adder4bit_1_cout), .DataOut(DataOut[3:0]));
  Adder4bit adder4bit_2 (
    .Data0(Data0[7:4]), .Data1(Data1[7:4]), .Cin(adder4bit_1_cout), .Cout(adder4bit_2_cout),
    .DataOut(DataOut[7:4]));
  Adder4bit adder4bit_3 (
    .Data0(Data0[11:8]), .Data1(Data1[11:8]), .Cin(adder4bit_2_cout), .Cout(Cout), .DataOut(DataOut[11:8]));
endmodule

// A19
module Adder19bit (
  input  Cin,
  input  [18:0] Data0,
  input  [18:0] Data1,
  output Cout,
  output [18:0] DataOut
);

  wire adder4bit_1_cout, adder4bit_2_cout, adder4bit_3_cout, adder4bit_4_cout;

  Adder4bit adder4bit_1 (
    .Data0(Data0[3:0]), .Data1(Data1[3:0]), .Cin(Cin), .Cout(adder4bit_1_cout), .DataOut(DataOut[3:0]));
  Adder4bit adder4bit_2 (
    .Data0(Data0[7:4]), .Data1(Data1[7:4]), .Cin(adder4bit_1_cout), .Cout(adder4bit_2_cout),
    .DataOut(DataOut[7:4]));
  Adder4bit adder4bit_3 (
    .Data0(Data0[11:8]), .Data1(Data1[11:8]), .Cin(adder4bit_2_cout), .Cout(adder4bit_3_cout),
    .DataOut(DataOut[11:8]));
  Adder4bit adder4bit_4 (
    .Data0(Data0[15:12]), .Data1(Data1[15:12]), .Cin(adder4bit_3_cout), .Cout(adder4bit_4_cout),
    .DataOut(DataOut[15:12]));
  Adder3bit adder3bit_1 (
    .Data0(Data0[18:16]), .Data1(Data1[18:16]), .Cin(adder4bit_4_cout), .Cout(Cout), .DataOut(DataOut[18:16]));
endmodule

// A22
module Adder22bit (
  input  Cin,
  input  [21:0] Data0,
  input  [21:0] Data1,
  output Cout,
  output [21:0] DataOut
);

  wire adder3bit_1_cout, adder4bit_1_cout, adder4bit_2_cout, adder4bit_3_cout, adder4bit_4_cout;

  Adder4bit adder4bit_1 (
    .Data0(Data0[3:0]), .Data1(Data1[3:0]), .Cin(Cin), .Cout(adder4bit_1_cout), .DataOut(DataOut[3:0]));
  Adder4bit adder4bit_2 (
    .Data0(Data0[7:4]), .Data1(Data1[7:4]), .Cin(adder4bit_1_cout), .Cout(adder4bit_2_cout),
    .DataOut(DataOut[7:4]));
  Adder4bit adder4bit_3 (
    .Data0(Data0[11:8]), .Data1(Data1[11:8]), .Cin(adder4bit_2_cout), .Cout(adder4bit_3_cout),
    .DataOut(DataOut[11:8]));
  Adder4bit adder4bit_4 (
    .Data0(Data0[15:12]), .Data1(Data1[15:12]), .Cin(adder4bit_3_cout), .Cout(adder4bit_4_cout),
    .DataOut(DataOut[15:12]));
  Adder3bit adder3bit_1 (
    .Data0(Data0[18:16]), .Data1(Data1[18:16]), .Cin(adder4bit_4_cout), .Cout(adder3bit_1_cout),
    .DataOut(DataOut[18:16]));
  Adder3bit adder3bit_2 (
    .Data0(Data0[21:19]), .Data1(Data1[21:19]), .Cin(adder3bit_1_cout), .Cout(Cout), .DataOut(DataOut[21:19]));
endmodule

// A25
module Adder25bit (
  input  Cin,
  input  [24:0] Data0,
  input  [24:0] Data1,
  output Cout,
  output [24:0] DataOut
);

  wire adder3bit_1_cout, adder3bit_2_cout, adder4bit_1_cout, adder4bit_2_cout, adder4bit_3_cout,
       adder4bit_4_cout;

  Adder4bit adder4bit_1 (
    .Data0(Data0[3:0]), .Data1(Data1[3:0]), .Cin(Cin), .Cout(adder4bit_1_cout), .DataOut(DataOut[3:0]));
  Adder4bit adder4bit_2 (
    .Data0(Data0[7:4]), .Data1(Data1[7:4]), .Cin(adder4bit_1_cout), .Cout(adder4bit_2_cout),
    .DataOut(DataOut[7:4]));
  Adder4bit adder4bit_3 (
    .Data0(Data0[11:8]), .Data1(Data1[11:8]), .Cin(adder4bit_2_cout), .Cout(adder4bit_3_cout),
    .DataOut(DataOut[11:8]));
  Adder4bit adder4bit_4 (
    .Data0(Data0[15:12]), .Data1(Data1[15:12]), .Cin(adder4bit_3_cout), .Cout(adder4bit_4_cout),
    .DataOut(DataOut[15:12]));
  Adder3bit adder3bit_1 (
    .Data0(Data0[18:16]), .Data1(Data1[18:16]), .Cin(adder4bit_4_cout), .Cout(adder3bit_1_cout),
    .DataOut(DataOut[18:16]));
  Adder3bit adder3bit_2 (
    .Data0(Data0[21:19]), .Data1(Data1[21:19]), .Cin(adder3bit_1_cout), .Cout(adder3bit_2_cout),
    .DataOut(DataOut[21:19]));
  Adder3bit adder3bit_3 (
    .Data0(Data0[24:22]), .Data1(Data1[24:22]), .Cin(adder3bit_2_cout), .Cout(Cout), .DataOut(DataOut[24:22]));
endmodule

// A28
module Adder28bit (
  input  Cin,
  input  [27:0] Data0,
  input  [27:0] Data1,
  output Cout,
  output [27:0] DataOut
);

  wire adder4bit_1_cout, adder4bit_2_cout, adder4bit_3_cout, adder4bit_4_cout, adder4bit_5_cout,
       adder4bit_6_cout;

  Adder4bit adder4bit_1 (
    .Data0(Data0[3:0]), .Data1(Data1[3:0]), .Cin(Cin), .Cout(adder4bit_1_cout), .DataOut(DataOut[3:0]));
  Adder4bit adder4bit_2 (
    .Data0(Data0[7:4]), .Data1(Data1[7:4]), .Cin(adder4bit_1_cout), .Cout(adder4bit_2_cout),
    .DataOut(DataOut[7:4]));
  Adder4bit adder4bit_3 (
    .Data0(Data0[11:8]), .Data1(Data1[11:8]), .Cin(adder4bit_2_cout), .Cout(adder4bit_3_cout),
    .DataOut(DataOut[11:8]));
  Adder4bit adder4bit_4 (
    .Data0(Data0[15:12]), .Data1(Data1[15:12]), .Cin(adder4bit_3_cout), .Cout(adder4bit_4_cout),
    .DataOut(DataOut[15:12]));
  Adder4bit adder4bit_5 (
    .Data0(Data0[19:16]), .Data1(Data1[19:16]), .Cin(adder4bit_4_cout), .Cout(adder4bit_5_cout),
    .DataOut(DataOut[19:16]));
  Adder4bit adder4bit_6 (
    .Data0(Data0[23:20]), .Data1(Data1[23:20]), .Cin(adder4bit_5_cout), .Cout(adder4bit_6_cout),
    .DataOut(DataOut[23:20]));
  Adder4bit adder4bit_7 (
    .Data0(Data0[27:24]), .Data1(Data1[27:24]), .Cin(adder4bit_6_cout), .Cout(Cout), .DataOut(DataOut[27:24]));
endmodule

// A31
module Adder31bit (
  input  Cin,
  input  [30:0] Data0,
  input  [30:0] Data1,
  output [30:0] DataOut,
  output Cout
);

  wire adder4bit_1_cout, adder4bit_2_cout, adder4bit_3_cout, adder4bit_4_cout, adder4bit_5_cout,
       adder4bit_6_cout, adder4bit_7_cout;

  Adder4bit adder4bit_1 (
    .Data0(Data0[3:0]), .Data1(Data1[3:0]), .Cin(Cin), .Cout(adder4bit_1_cout), .DataOut(DataOut[3:0]));
  Adder4bit adder4bit_2 (
    .Data0(Data0[7:4]), .Data1(Data1[7:4]), .Cin(adder4bit_1_cout), .Cout(adder4bit_2_cout),
    .DataOut(DataOut[7:4]));
  Adder4bit adder4bit_3 (
    .Data0(Data0[11:8]), .Data1(Data1[11:8]), .Cin(adder4bit_2_cout), .Cout(adder4bit_3_cout),
    .DataOut(DataOut[11:8]));
  Adder4bit adder4bit_4 (
    .Data0(Data0[15:12]), .Data1(Data1[15:12]), .Cin(adder4bit_3_cout), .Cout(adder4bit_4_cout),
    .DataOut(DataOut[15:12]));
  Adder4bit adder4bit_5 (
    .Data0(Data0[19:16]), .Data1(Data1[19:16]), .Cin(adder4bit_4_cout), .Cout(adder4bit_5_cout),
    .DataOut(DataOut[19:16]));
  Adder4bit adder4bit_6 (
    .Data0(Data0[23:20]), .Data1(Data1[23:20]), .Cin(adder4bit_5_cout), .Cout(adder4bit_6_cout),
    .DataOut(DataOut[23:20]));
  Adder4bit adder4bit_7 (
    .Data0(Data0[27:24]), .Data1(Data1[27:24]), .Cin(adder4bit_6_cout), .Cout(adder4bit_7_cout),
    .DataOut(DataOut[27:24]));
  Adder3bit adder3bit_1 (
    .Data0(Data0[30:28]), .Data1(Data1[30:28]), .Cin(adder4bit_7_cout), .Cout(Cout), .DataOut(DataOut[30:28]));
endmodule

// A32
module Adder32bit (
  input  Cin,
  input  [31:0] Data0,
  input  [31:0] Data1,
  output [31:0] DataOut,
  output Cout
);

  wire adder4bit_1_cout, adder4bit_2_cout, adder4bit_3_cout, adder4bit_4_cout, adder4bit_5_cout,
       adder4bit_6_cout, adder4bit_7_cout;

  Adder4bit adder4bit_1 (
    .Data0(Data0[3:0]), .Data1(Data1[3:0]), .Cin(Cin), .Cout(adder4bit_1_cout), .DataOut(DataOut[3:0]));
  Adder4bit adder4bit_2 (
    .Data0(Data0[7:4]), .Data1(Data1[7:4]), .Cin(adder4bit_1_cout), .Cout(adder4bit_2_cout),
    .DataOut(DataOut[7:4]));
  Adder4bit adder4bit_3 (
    .Data0(Data0[11:8]), .Data1(Data1[11:8]), .Cin(adder4bit_2_cout), .Cout(adder4bit_3_cout),
    .DataOut(DataOut[11:8]));
  Adder4bit adder4bit_4 (
    .Data0(Data0[15:12]), .Data1(Data1[15:12]), .Cin(adder4bit_3_cout), .Cout(adder4bit_4_cout),
    .DataOut(DataOut[15:12]));
  Adder4bit adder4bit_5 (
    .Data0(Data0[19:16]), .Data1(Data1[19:16]), .Cin(adder4bit_4_cout), .Cout(adder4bit_5_cout),
    .DataOut(DataOut[19:16]));
  Adder4bit adder4bit_6 (
    .Data0(Data0[23:20]), .Data1(Data1[23:20]), .Cin(adder4bit_5_cout), .Cout(adder4bit_6_cout),
    .DataOut(DataOut[23:20]));
  Adder4bit adder4bit_7 (
    .Data0(Data0[27:24]), .Data1(Data1[27:24]), .Cin(adder4bit_6_cout), .Cout(adder4bit_7_cout),
    .DataOut(DataOut[27:24]));
  Adder4bit adder4bit_8 (
    .Data0(Data0[31:28]), .Data1(Data1[31:28]), .Cin(adder4bit_7_cout), .Cout(Cout), .DataOut(DataOut[31:28]));
endmodule

// XOR4
module XOR4bit2x1 (
  input  [3:0] Data0,
  input  [3:0] Data1,
  output [3:0] DataOut
);

  // _7486 7486_1: pin names not known; wires that end beside it: Data0[0], Data1[0], DataOut[0], Data0[1], Data1[1], DataOut[1], 1'b0, 1'b1, Data0[3], Data1[3], DataOut[3], Data0[2], Data1[2], DataOut[2]
endmodule

// XOR3
module XOR3bit2x1 (
  input  [2:0] Data0,
  input  [2:0] Data1,
  output [2:0] DataOut
);

  wire n7486_1_p9, n7486_1_p10, n7486_1_p11;

  // _7486 7486_1: pin names not known; wires that end beside it: Data0[0], Data1[0], DataOut[0], Data0[1], Data1[1], DataOut[1], 1'b0, 1'b1, n7486_1_p9, n7486_1_p10, n7486_1_p11, Data0[2], Data1[2], DataOut[2], n7486_1_p9, n7486_1_p10, n7486_1_p11
endmodule

// XOR12
module XOR12bit2x1 (
  input  [11:0] Data0,
  input  [11:0] Data1,
  output [11:0] DataOut
);

  XOR4bit2x1 xor4bit2x1_1 (.Data0(Data0[3:0]), .Data1(Data1[3:0]), .DataOut(DataOut[3:0]));
  XOR4bit2x1 xor4bit2x1_2 (.Data0(Data0[7:4]), .Data1(Data1[7:4]), .DataOut(DataOut[7:4]));
  XOR4bit2x1 xor4bit2x1_3 (.Data0(Data0[11:8]), .Data1(Data1[11:8]), .DataOut(DataOut[11:8]));
endmodule

// XOR19
module XOR19bit2x1 (
  input  [18:0] Data0,
  input  [18:0] Data1,
  output [18:0] DataOut
);

  XOR4bit2x1 xor4bit2x1_1 (.Data0(Data0[3:0]), .Data1(Data1[3:0]), .DataOut(DataOut[3:0]));
  XOR4bit2x1 xor4bit2x1_2 (.Data0(Data0[7:4]), .Data1(Data1[7:4]), .DataOut(DataOut[7:4]));
  XOR4bit2x1 xor4bit2x1_3 (.Data0(Data0[11:8]), .Data1(Data1[11:8]), .DataOut(DataOut[11:8]));
  XOR4bit2x1 xor4bit2x1_4 (.Data0(Data0[15:12]), .Data1(Data1[15:12]), .DataOut(DataOut[15:12]));
  XOR3bit2x1 xor3bit2x1_1 (.Data0(Data0[18:16]), .Data1(Data1[18:16]), .DataOut(DataOut[18:16]));
endmodule

// XOR32
module XOR32bit2x1 (
  input  [31:0] Data0,
  input  [31:0] Data1,
  output [31:0] DataOut
);

  XOR4bit2x1 xor4bit2x1_1 (.Data0(Data0[3:0]), .Data1(Data1[3:0]), .DataOut(DataOut[3:0]));
  XOR4bit2x1 xor4bit2x1_2 (.Data0(Data0[7:4]), .Data1(Data1[7:4]), .DataOut(DataOut[7:4]));
  XOR4bit2x1 xor4bit2x1_3 (.Data0(Data0[11:8]), .Data1(Data1[11:8]), .DataOut(DataOut[11:8]));
  XOR4bit2x1 xor4bit2x1_4 (.Data0(Data0[15:12]), .Data1(Data1[15:12]), .DataOut(DataOut[15:12]));
  XOR4bit2x1 xor4bit2x1_5 (.Data0(Data0[19:16]), .Data1(Data1[19:16]), .DataOut(DataOut[19:16]));
  XOR4bit2x1 xor4bit2x1_6 (.Data0(Data0[23:20]), .Data1(Data1[23:20]), .DataOut(DataOut[23:20]));
  XOR4bit2x1 xor4bit2x1_7 (.Data0(Data0[27:24]), .Data1(Data1[27:24]), .DataOut(DataOut[27:24]));
  XOR4bit2x1 xor4bit2x1_8 (.Data0(Data0[31:28]), .Data1(Data1[31:28]), .DataOut(DataOut[31:28]));
endmodule

// NOT1
module NOT1bit (
  input  A,
  output A_prime
);

  // _7404 7404_1: pin names not known; wires that end beside it: A, A_prime, 1'b0, 1'b1
endmodule

// NOT3
module NOT3bit (
  input  [2:0] Data0,
  output [2:0] DataOut
);

  // _7404 7404_1: pin names not known; wires that end beside it: Data0[0], DataOut[0], Data0[1], DataOut[1], Data0[2], DataOut[2], 1'b0, 1'b1
endmodule

// NOT4
module NOT4bit (
  input  [3:0] Data0,
  output [3:0] DataOut
);

  // _7404 7404_1: pin names not known; wires that end beside it: Data0[0], DataOut[0], Data0[1], DataOut[1], Data0[2], DataOut[2], 1'b0, 1'b1, Data0[3], DataOut[3]
endmodule

// NOT12
module NOT12bit (
  input  [11:0] Data0,
  output [11:0] DataOut
);

  NOT4bit not4bit_1 (.Data0(Data0[3:0]), .DataOut(DataOut[3:0]));
  NOT4bit not4bit_2 (.Data0(Data0[7:4]), .DataOut(DataOut[7:4]));
  NOT4bit not4bit_3 (.Data0(Data0[11:8]), .DataOut(DataOut[11:8]));
endmodule

// Zero
module Zero32bit (
  output [31:0] out_1
);


  assign out_1 = {32{1'b0}};
endmodule

// NOT19
module NOT19bit (
  input  [18:0] Data0,
  output [18:0] DataOut
);

  NOT4bit not4bit_1 (.Data0(Data0[3:0]), .DataOut(DataOut[3:0]));
  NOT4bit not4bit_2 (.Data0(Data0[7:4]), .DataOut(DataOut[7:4]));
  NOT4bit not4bit_3 (.Data0(Data0[11:8]), .DataOut(DataOut[11:8]));
  NOT4bit not4bit_4 (.Data0(Data0[15:12]), .DataOut(DataOut[15:12]));
  NOT3bit not3bit_1 (.Data0(Data0[18:16]), .DataOut(DataOut[18:16]));
endmodule

// M1
module MUX1bit2x1 (
  input  S,
  input  Data0,
  input  Data1,
  output DataOut
);

  wire n74157_1_p8, n74157_1_p9, n74157_1_p10;

  // _74157 74157_1: pin names not known; wires that end beside it: S, Data0, Data1, DataOut, 1'b0, 1'b1, 1'b0, n74157_1_p8, n74157_1_p9, n74157_1_p10, n74157_1_p8, n74157_1_p9, n74157_1_p10
endmodule

// XOR1
module XOR1bit2x1 (
  input  Data0,
  input  Data1,
  output DataOut
);

  wire n7486_1_p6, n7486_1_p7, n7486_1_p8;

  // _7486 7486_1: pin names not known; wires that end beside it: Data0, Data1, DataOut, 1'b0, 1'b1, n7486_1_p6, n7486_1_p7, n7486_1_p8, n7486_1_p6, n7486_1_p7, n7486_1_p8
endmodule

module _4bitLeftShifter (
  input  [3:0] in,
  input  [3:0] shamt,
  output [3:0] out
);

  wire or1bit2x1_1_out_2;
  wire [3:0] mux4bit2x1_1_dataout, mux4bit2x1_2_dataout;

  MUX4bit2x1 mux4bit2x1_1 (.S(shamt[0]), .Data0(in), .Data1({in[2:0], 1'b0}), .DataOut(mux4bit2x1_1_dataout));
  OR1bit2x1 or1bit2x1_1 (.in_1(shamt[3:2]), .out_2(or1bit2x1_1_out_2));
  MUX4bit2x1 mux4bit2x1_2 (
    .S(shamt[1]), .Data0(mux4bit2x1_1_dataout), .Data1({mux4bit2x1_1_dataout[1:0], 2'b00}),
    .DataOut(mux4bit2x1_2_dataout));
  MUX4bit2x1 mux4bit2x1_3 (.S(or1bit2x1_1_out_2), .Data0(mux4bit2x1_2_dataout), .Data1(4'b0000), .DataOut(out));
endmodule

module _4bitRightShifter (
  input  [3:0] in,
  input  [3:0] shamt,
  output [3:0] out
);

  wire or1bit2x1_1_out_2;
  wire [3:0] mux4bit2x1_1_dataout, mux4bit2x1_2_dataout;

  MUX4bit2x1 mux4bit2x1_1 (.S(shamt[0]), .Data0(in), .Data1({{2{in[3]}}, in[2:1]}), .DataOut(mux4bit2x1_1_dataout));
  OR1bit2x1 or1bit2x1_1 (.in_1(shamt[3:2]), .out_2(or1bit2x1_1_out_2));
  MUX4bit2x1 mux4bit2x1_2 (
    .S(shamt[1]), .Data0(mux4bit2x1_1_dataout), .Data1({{2{in[3]}}, mux4bit2x1_1_dataout[3:2]}),
    .DataOut(mux4bit2x1_2_dataout));
  MUX4bit2x1 mux4bit2x1_3 (.S(or1bit2x1_1_out_2), .Data0(mux4bit2x1_2_dataout), .Data1({4{in[3]}}), .DataOut(out));
endmodule
